# Fritzing sketch sketch-fritzing (saved by Fritzing 0.9.3b)

parts:
  Arduino_Nano = Arduino Nano (Rev3.0)
  RTC = Real Time Clock Module - DS1307 RTC Breakout Board
  R1 = Resistor [tolerance=±5% resistance=220 package=THT]
  LED_Status = LED - 3mm [color="Green (570nm)" package="3 mm [THT]"]
  Pulldown = Resistor [tolerance=±5% resistance=10k package=THT]
  USB_Connector_to_PULZAR_LED_HO = USB+SHIELD [package=usb-b-pth]
  Switch_Maintenance_Mode = SWITCH-SPST-2 [package=switch-spst-vertical]
  LED_Maintenance_Mode = LED - 3mm [color="Blue (505nm)" package="3 mm [THT]"]
  R3 = Resistor [tolerance=±5% resistance=220 package=THT]

nets:
  GND: Arduino_Nano.GND, RTC.GND, LED_Status.anode, Pulldown.Pin_1, USB_Connector_to_PULZAR_LED_HO.P$1, USB_Connector_to_PULZAR_LED_HO.P$2, LED_Maintenance_Mode.anode
  N1: Arduino_Nano.D5, USB_Connector_to_PULZAR_LED_HO.VBUS
  N2: Arduino_Nano.D6, USB_Connector_to_PULZAR_LED_HO.D+
  N3: Arduino_Nano.D7, Pulldown.Pin_0, Switch_Maintenance_Mode.P, R3.Pin_1
  N4: Arduino_Nano.D9, USB_Connector_to_PULZAR_LED_HO.D-
  5V: Arduino_Nano.5V, RTC.5V, Switch_Maintenance_Mode.O
  N5: Arduino_Nano.A5, RTC.SCL
  N6: Arduino_Nano.A4, RTC.SDA
  N7: Arduino_Nano.D13/SCK, R1.Pin_0
  N8: R1.Pin_1, LED_Status.cathode
  N9: LED_Maintenance_Mode.cathode, R3.Pin_0
